# Fritzing sketch Controller (saved by Fritzing 0.9.3b)
circuit board: 3.79999cm x 4.09999cm
breadboards: 1

parts:
  C1 = Ceramic Capacitor [capacitance=22pF package="100 mil [THT, multilayer]"]
  C2 = Ceramic Capacitor [capacitance=22pF package="100 mil [THT, multilayer]"]
  R4 = Resistor [tolerance=±5% resistance=10k package=THT]
  Q1 = NPN-Transistor [part_number=2N3904 package="TO92 [THT]"]
  Q2 = NPN-Transistor [package="TO92 [THT]"]
  R5 = Resistor [tolerance=±5% resistance=10k package=THT]
  U4 = Voltage Regulator - 5V [package="TO220 [THT]"]
  R6 = Resistor [tolerance=±5% resistance=330 package=THT]
  R3 = Resistor [tolerance=±5% resistance=1k package=THT]
  XTAL1 = Crystal [frequency="16 Mhz" package=THT]
  U1 = atmega328 [package=dip]
  C3 = Electrolytic Capacitor [capacitance=1µF package="100 mil [THT, electrolytic]"]  # not connected
  C4 = Electrolytic Capacitor [capacitance=1µF package="100 mil [THT, electrolytic]"]  # not connected

nets:
  N1: C1.0, XTAL1.pin_0, U1.XLAT2
  N2: C1.1, C2.0, Q1.E, Q2.C, U4.GND, U1.GND#7
  N3: C2.1, XTAL1.pin_1, U1.XLAT1
  N4: R4.Pin_0, Q1.C, R3.Pin_1
  N5: R4.Pin_1, Q2.B
  N6: Q1.B, R6.Pin_1
  N7: Q2.E, R5.Pin_0, U1.D2
  N8: R5.Pin_1, U4.output_voltage, U1.VCC
  N9: U4.input_voltage, R3.Pin_0
  N10: R6.Pin_0, U1.A5

notes:
  GND
  D+
  D-
  5V
  IO
  K
  L
  VCC
