# Fritzing sketch Operator_Device (saved by Fritzing 0.9.3b)
circuit board: 8.28916cm x 6.47594cm
breadboards: 1

parts:
  R1 = Trimmer Potentiometer [maximum_resistance=1kΩ package=THT]
  X1 = USB Connectors [package=usb-a-s]
  C2 = Capacitor [package=cap-pth-small2]
  C1 = Capacitor [package=cap-pth-small2]
  U1 = atmega328 [package=dip]
  S3 = SWITCH-MOMENTARY-2 [package=tactile-pth-12mm]
  S2 = SWITCH-MOMENTARY-2 [package=tactile-pth-12mm]
  LCD1 = LCD screen
  XTAL1 = Crystal [frequency="16 Mhz" package=THT]
  J1 = female pin header, 1 pin [form="♀ (female)"]
  S4 = SWITCH-MOMENTARY-2 [package=tactile-pth-12mm]

nets:
  GND: R1.leg1, X1.GND, C1.2, U1.GND#21, S3.1, S2.1, LCD1.VSS, LCD1.R/W, LCD1.LED-, S4.1
  N1: R1.wiper, LCD1.V0
  VCC: R1.leg2, U1.VCC, LCD1.VDD, LCD1.LED+
  N2: X1.D+, U1.D0_(RX)
  N3: X1.D-, U1.D1_(TX)
  N4: C2.1, U1.GND#7
  N5: C2.2, U1.XLAT1, XTAL1.pin_0
  N6: C1.1, U1.XLAT2, XTAL1.pin_1
  N7: U1.RESET, J1.pin1
  N8: U1.D2, S4.2
  N9: U1.D3_(PWM), S2.2
  N10: U1.D4, S3.2
  N11: U1.D12, LCD1.RS
  N12: U1.D13, LCD1.E
  N13: U1.A2, LCD1.DB4
  N14: U1.A3, LCD1.DB5
  N15: U1.A4, LCD1.DB6
  N16: U1.A5, LCD1.DB7
